// Logisim project 00_ALTER_SMART_COMPLETO.circ as structural Verilog: 7 circuits, main circuit main
module main (
  input  PRESENCA,
  input  ESCURO,
  input  MANUAL,
  input  ARMADO,
  input  PORTA,
  input  JANELA,
  input  MOVIMENTO,
  input  [3:0] QTD,
  input  [3:0] MIN,
  input  [4:0] T,
  input  [4:0] SET,
  input  PRESENCA_AR,
  output LUZ,
  output S1,
  output S0,
  output SOLICITADO,
  output ACEITO,
  output ANDAMENTO,
  output CONCLUIDO,
  output SIRENE,
  output AVISO_ABERTA,
  output BAIXO,
  output OK,
  output COMPRESSOR,
  output NO_ALVO
);

  wire AVANCAR_out, RESET_out;

  luz_automatica luz_automatica_1 (.PRESENCA(PRESENCA), .ESCURO(ESCURO), .MANUAL(MANUAL), .LUZ(LUZ));
  alarme alarme_1 (
    .ARMADO(ARMADO), .PORTA(PORTA), .JANELA(JANELA), .MOVIMENTO(MOVIMENTO), .SIRENE(SIRENE),
    .AVISO_ABERTA(AVISO_ABERTA));
  alerta_estoque alerta_estoque_1 (.QTD(QTD), .MIN(MIN), .BAIXO(BAIXO), .OK(OK));
  termostato termostato_1 (.T(T), .SET(SET), .PRESENCA(PRESENCA_AR), .COMPRESSOR(COMPRESSOR), .NO_ALVO(NO_ALVO));
  LED LUZ_LED (.in(LUZ));
  LED SIRENE_LED (.in(SIRENE));
  LED AVISO_ABERTA_LED (.in(AVISO_ABERTA));
  LED BAIXO_LED (.in(BAIXO));
  LED OK_LED (.in(OK));
  LED COMPRESSOR_LED (.in(COMPRESSOR));
  LED NO_ALVO_LED (.in(NO_ALVO));
  Button AVANCAR (.out(AVANCAR_out));
  Button RESET (.out(RESET_out));
  maquina_pedido maquina_pedido_1 (
    .CLK(AVANCAR_out), .RESET(RESET_out), .S1(S1), .S0(S0), .SOLICITADO(SOLICITADO), .ACEITO(ACEITO),
    .ANDAMENTO(ANDAMENTO), .CONCLUIDO(CONCLUIDO));
  LED S1_LED (.in(S1));
  LED S0_LED (.in(S0));
  LED SOLICITADO_LED (.in(SOLICITADO));
  LED ACEITO_LED (.in(ACEITO));
  LED ANDAMENTO_LED (.in(ANDAMENTO));
  LED CONCLUIDO_LED (.in(CONCLUIDO));

  // Notes on the sheet:
  //   ALTER SMART // PAINEL DA CASA INTELIGENTE  (Logisim-evolution 4.1.0)
  //   Use a ferramenta Cutucar (mao) para mudar as entradas. Os blocos sao subcircuitos: clique 2x para ver por dentro.
  //   1) LUZ AUTOMATICA  - sensor de presenca + escuro, ou interruptor do app
  //   2) ALARME - arme e abra porta/janela ou gere movimento
  //   3) ESTOQUE - QTD e MIN em binario (4 bits)
  //   4) TERMOSTATO - T e SET em graus C (5 bits)
  //   5) STATUS DO PEDIDO - aperte AVANCAR (pulso de clock)
endmodule

module luz_automatica (
  input  PRESENCA,
  input  ESCURO,
  input  MANUAL,
  output LUZ
);

  wire and_1_out;

  and and_1 (and_1_out, PRESENCA, ESCURO);
  or or_1 (LUZ, and_1_out, MANUAL);
  LED LUZ_LED (.in(LUZ));

  // Notes on the sheet:
  //   ALTER SMART // 01 - LUZ AUTOMATICA
  //   LUZ = (PRESENCA . ESCURO) + MANUAL   |  sensor PIR + LDR + interruptor do app
endmodule

module alarme (
  input  ARMADO,
  input  PORTA,
  input  JANELA,
  input  MOVIMENTO,
  output SIRENE,
  output AVISO_ABERTA
);

  wire not_1_out, or_1_out, or_2_out;

  or or_1 (or_1_out, PORTA, JANELA, MOVIMENTO);
  or or_2 (or_2_out, PORTA, JANELA);
  not not_1 (not_1_out, ARMADO);
  and and_1 (SIRENE, ARMADO, or_1_out);
  and and_2 (AVISO_ABERTA, or_2_out, not_1_out);
  LED SIRENE_LED (.in(SIRENE));
  LED AVISO_ABERTA_LED (.in(AVISO_ABERTA));

  // Notes on the sheet:
  //   ALTER SMART // 02 - ALARME RESIDENCIAL
  //   SIRENE = ARMADO . (PORTA + JANELA + MOVIMENTO)    AVISO = /ARMADO . (PORTA + JANELA)
endmodule

module alerta_estoque (
  input  [3:0] QTD,
  input  [3:0] MIN,
  output OK,
  output BAIXO
);

  wire comparator_1_eq, comparator_1_lt;

  Comparator #(.width(4), .mode("unsigned")) comparator_1 (
    .a(QTD), .b(MIN), .gt(OK), .eq(comparator_1_eq), .lt(comparator_1_lt));
  or or_1 (BAIXO, comparator_1_eq, comparator_1_lt);
  LED OK_LED (.in(OK));
  LED BAIXO_LED (.in(BAIXO));

  // Notes on the sheet:
  //   ALTER SMART // 03 - ALERTA DE ESTOQUE
  //   BAIXO = (QTD < MIN) + (QTD = MIN)   ->  mesma regra do banco: quantidade <= quantidade_minima
endmodule

module termostato (
  input  [4:0] T,
  input  [4:0] SET,
  input  PRESENCA,
  output COMPRESSOR,
  output NO_ALVO
);

  wire comparator_1_gt;

  Comparator #(.width(5), .mode("unsigned")) comparator_1 (
    .a(T), .b(SET), .gt(comparator_1_gt), .eq(NO_ALVO));  // open: lt
  and and_1 (COMPRESSOR, comparator_1_gt, PRESENCA);
  LED COMPRESSOR_LED (.in(COMPRESSOR));
  LED NO_ALVO_LED (.in(NO_ALVO));

  // Notes on the sheet:
  //   ALTER SMART // 04 - TERMOSTATO DO AR-CONDICIONADO
  //   COMPRESSOR = (T > SET) . PRESENCA   |   NO_ALVO = (T = SET)   |   T e SET em graus C (0 a 31)
endmodule

module maquina_pedido (
  input  CLK,
  input  RESET,
  output S1,
  output S0,
  output SOLICITADO,
  output ACEITO,
  output ANDAMENTO,
  output CONCLUIDO
);

  wire and_1_out, and_2_out, INC, NS0, NS1, xor_1_out, xor_2_out;

  and and_1 (and_1_out, S1, S0);
  not not_1 (INC, and_1_out);
  not not_2 (NS1, S1);
  not not_3 (NS0, S0);
  xor xor_1 (xor_1_out, S0, INC);
  and and_2 (and_2_out, S0, INC);
  D_Flip_Flop FF_S0 (.D(xor_1_out), .clk(CLK), .Q(S0), .reset(RESET));  // open: Qn, preset
  D_Flip_Flop FF_S1 (.D(xor_2_out), .clk(CLK), .Q(S1), .reset(RESET));  // open: Qn, preset
  xor xor_2 (xor_2_out, S1, and_2_out);
  and and_3 (SOLICITADO, NS1, NS0);
  and and_4 (ACEITO, NS1, S0);
  and and_5 (ANDAMENTO, S1, NS0);
  and and_6 (CONCLUIDO, S1, S0);
  LED SOLICITADO_LED (.in(SOLICITADO));
  LED ACEITO_LED (.in(ACEITO));
  LED ANDAMENTO_LED (.in(ANDAMENTO));
  LED CONCLUIDO_LED (.in(CONCLUIDO));

  // Notes on the sheet:
  //   ALTER SMART // 06 - MAQUINA DE ESTADOS DO PEDIDO (2 flip-flops D)
  //   Cada pulso em CLK avanca o status: 00 Solicitado -> 01 Aceito -> 10 Em andamento -> 11 Concluido (para no 11). RESET volta ao 00.
  //   Decodificador 2->4 (status atual)
endmodule

module logica_pedido (
  input  S1,
  input  S0,
  input  AVANCAR,
  output N0,
  output N1,
  output SOLICITADO,
  output ACEITO,
  output ANDAMENTO,
  output CONCLUIDO
);

  wire and_1_out, and_3_out, INC, not_1_out, NS0, NS1;

  and and_1 (and_1_out, S1, S0);
  not not_1 (not_1_out, and_1_out);
  and and_2 (INC, not_1_out, AVANCAR);
  not not_2 (NS1, S1);
  not not_3 (NS0, S0);
  and and_3 (and_3_out, S0, INC);
  and and_4 (SOLICITADO, NS1, NS0);
  and and_5 (ACEITO, NS1, S0);
  and and_6 (ANDAMENTO, S1, NS0);
  and and_7 (CONCLUIDO, S1, S0);
  xor xor_1 (N0, S0, INC);
  xor xor_2 (N1, S1, and_3_out);
  LED SOLICITADO_LED (.in(SOLICITADO));
  LED ACEITO_LED (.in(ACEITO));
  LED ANDAMENTO_LED (.in(ANDAMENTO));
  LED CONCLUIDO_LED (.in(CONCLUIDO));

  // Notes on the sheet:
  //   ALTER SMART // 05 - STATUS DO PEDIDO (logica de proximo estado + decodificador)
  //   00 Solicitado -> 01 Aceito -> 10 Em andamento -> 11 Concluido.  So avanca (igual a API PUT /pedidos/:id)
  //   Decodificador 2->4 (status atual)
endmodule
