// Logisim project 01_luz_automatica.circ as structural Verilog: 1 circuit, main circuit main
module main (
  input  PRESENCA,
  input  ESCURO,
  input  MANUAL,
  output LUZ
);

  wire and_1_out;

  and and_1 (and_1_out, PRESENCA, ESCURO);
  or or_1 (LUZ, and_1_out, MANUAL);
  LED LUZ_LED (.in(LUZ));

  // Notes on the sheet:
  //   ALTER SMART // 01 - LUZ AUTOMATICA
  //   LUZ = (PRESENCA . ESCURO) + MANUAL   |  sensor PIR + LDR + interruptor do app
endmodule
