// Logisim project 02_alarme_seguranca.circ as structural Verilog: 1 circuit, main circuit main
module main (
  input  ARMADO,
  input  PORTA,
  input  JANELA,
  input  MOVIMENTO,
  output SIRENE,
  output AVISO_ABERTA
);

  wire not_1_out, or_1_out, or_2_out;

  or or_1 (or_1_out, PORTA, JANELA, MOVIMENTO);
  or or_2 (or_2_out, PORTA, JANELA);
  not not_1 (not_1_out, ARMADO);
  and and_1 (SIRENE, ARMADO, or_1_out);
  and and_2 (AVISO_ABERTA, or_2_out, not_1_out);
  LED SIRENE_LED (.in(SIRENE));
  LED AVISO_ABERTA_LED (.in(AVISO_ABERTA));

  // Notes on the sheet:
  //   ALTER SMART // 02 - ALARME RESIDENCIAL
  //   SIRENE = ARMADO . (PORTA + JANELA + MOVIMENTO)    AVISO = /ARMADO . (PORTA + JANELA)
endmodule
