// Logisim project 03_alerta_estoque.circ as structural Verilog: 1 circuit, main circuit main
module main (
  input  [3:0] QTD,
  input  [3:0] MIN,
  output OK,
  output BAIXO
);

  wire comparator_1_eq, comparator_1_lt;

  Comparator #(.width(4), .mode("unsigned")) comparator_1 (
    .a(QTD), .b(MIN), .gt(OK), .eq(comparator_1_eq), .lt(comparator_1_lt));
  or or_1 (BAIXO, comparator_1_eq, comparator_1_lt);
  LED OK_LED (.in(OK));
  LED BAIXO_LED (.in(BAIXO));

  // Notes on the sheet:
  //   ALTER SMART // 03 - ALERTA DE ESTOQUE
  //   BAIXO = (QTD < MIN) + (QTD = MIN)   ->  mesma regra do banco: quantidade <= quantidade_minima
endmodule
