// Logisim project 04_termostato.circ as structural Verilog: 1 circuit, main circuit main
module main (
  input  [4:0] T,
  input  [4:0] SET,
  input  PRESENCA,
  output COMPRESSOR,
  output NO_ALVO
);

  wire comparator_1_gt;

  Comparator #(.width(5), .mode("unsigned")) comparator_1 (
    .a(T), .b(SET), .gt(comparator_1_gt), .eq(NO_ALVO));  // open: lt
  and and_1 (COMPRESSOR, comparator_1_gt, PRESENCA);
  LED COMPRESSOR_LED (.in(COMPRESSOR));
  LED NO_ALVO_LED (.in(NO_ALVO));

  // Notes on the sheet:
  //   ALTER SMART // 04 - TERMOSTATO DO AR-CONDICIONADO
  //   COMPRESSOR = (T > SET) . PRESENCA   |   NO_ALVO = (T = SET)   |   T e SET em graus C (0 a 31)
endmodule
