// Logisim project 05_status_pedido.circ as structural Verilog: 1 circuit, main circuit main
module main (
  input  S1,
  input  S0,
  input  AVANCAR,
  output N0,
  output N1,
  output SOLICITADO,
  output ACEITO,
  output ANDAMENTO,
  output CONCLUIDO
);

  wire and_1_out, and_3_out, INC, not_1_out, NS0, NS1;

  and and_1 (and_1_out, S1, S0);
  not not_1 (not_1_out, and_1_out);
  and and_2 (INC, not_1_out, AVANCAR);
  not not_2 (NS1, S1);
  not not_3 (NS0, S0);
  and and_3 (and_3_out, S0, INC);
  and and_4 (SOLICITADO, NS1, NS0);
  and and_5 (ACEITO, NS1, S0);
  and and_6 (ANDAMENTO, S1, NS0);
  and and_7 (CONCLUIDO, S1, S0);
  xor xor_1 (N0, S0, INC);
  xor xor_2 (N1, S1, and_3_out);
  LED SOLICITADO_LED (.in(SOLICITADO));
  LED ACEITO_LED (.in(ACEITO));
  LED ANDAMENTO_LED (.in(ANDAMENTO));
  LED CONCLUIDO_LED (.in(CONCLUIDO));

  // Notes on the sheet:
  //   ALTER SMART // 05 - STATUS DO PEDIDO (logica de proximo estado + decodificador)
  //   00 Solicitado -> 01 Aceito -> 10 Em andamento -> 11 Concluido.  So avanca (igual a API PUT /pedidos/:id)
  //   Decodificador 2->4 (status atual)
endmodule
