// Logisim project 06_maquina_pedido.circ as structural Verilog: 1 circuit, main circuit main
module main (
  input  CLK,
  input  RESET,
  output S1,
  output S0,
  output SOLICITADO,
  output ACEITO,
  output ANDAMENTO,
  output CONCLUIDO
);

  wire and_1_out, and_2_out, INC, NS0, NS1, xor_1_out, xor_2_out;

  and and_1 (and_1_out, S1, S0);
  not not_1 (INC, and_1_out);
  not not_2 (NS1, S1);
  not not_3 (NS0, S0);
  xor xor_1 (xor_1_out, S0, INC);
  and and_2 (and_2_out, S0, INC);
  D_Flip_Flop FF_S0 (.D(xor_1_out), .clk(CLK), .Q(S0), .reset(RESET));  // open: Qn, preset
  D_Flip_Flop FF_S1 (.D(xor_2_out), .clk(CLK), .Q(S1), .reset(RESET));  // open: Qn, preset
  xor xor_2 (xor_2_out, S1, and_2_out);
  and and_3 (SOLICITADO, NS1, NS0);
  and and_4 (ACEITO, NS1, S0);
  and and_5 (ANDAMENTO, S1, NS0);
  and and_6 (CONCLUIDO, S1, S0);
  LED SOLICITADO_LED (.in(SOLICITADO));
  LED ACEITO_LED (.in(ACEITO));
  LED ANDAMENTO_LED (.in(ANDAMENTO));
  LED CONCLUIDO_LED (.in(CONCLUIDO));

  // Notes on the sheet:
  //   ALTER SMART // 06 - MAQUINA DE ESTADOS DO PEDIDO (2 flip-flops D)
  //   Cada pulso em CLK avanca o status: 00 Solicitado -> 01 Aceito -> 10 Em andamento -> 11 Concluido (para no 11). RESET volta ao 00.
  //   Decodificador 2->4 (status atual)
endmodule
